// Logisim project 2_input_mux.circ as structural Verilog: 1 circuit, main circuit two_input_mux
module two_input_mux (
  input  sel,
  input  input0,
  input  input1,
  output out_4
);

  wire and_1_out, and_2_out, not_1_out;

  not not_1 (not_1_out, sel);
  and and_1 (and_1_out, not_1_out, input0);
  and and_2 (and_2_out, sel, input1);
  or or_1 (out_4, and_1_out, and_2_out);
endmodule
