// Logisim project 4_bit_ALU.circ as structural Verilog: 1 circuit, main circuit four_input_ALU
module four_input_ALU (
  input  control0,
  input  control1,
  input  a0,
  input  b0,
  input  a1,
  input  b1,
  input  a2,
  input  b2,
  input  a3,
  input  b3,
  output result0,
  output result1,
  output result2,
  output result3,
  output carryout
);

  wire and_1_out, and_2_out, and_3_out, and_4_out, four_bit_adder_1_result0, four_bit_adder_1_result1,
       four_bit_adder_1_result2, four_bit_adder_1_result3, not_1_out, not_2_out, not_3_out, not_4_out,
       not_5_out, not_6_out, not_7_out, not_8_out, or_1_out, or_2_out, or_3_out, or_4_out,
       two_input_mux_1_out_4, two_input_mux_2_out_4, two_input_mux_3_out_4, two_input_mux_4_out_4;

  not not_1 (not_1_out, b0);
  not not_2 (not_2_out, b1);
  not not_3 (not_3_out, b2);
  not not_4 (not_4_out, b3);
  two_input_mux two_input_mux_1 (.sel(b0), .input0(b0), .input1(not_1_out), .out_4(two_input_mux_1_out_4));
  two_input_mux two_input_mux_2 (.sel(b0), .input0(b1), .input1(not_2_out), .out_4(two_input_mux_2_out_4));
  two_input_mux two_input_mux_3 (.sel(b0), .input0(b2), .input1(not_3_out), .out_4(two_input_mux_3_out_4));
  two_input_mux two_input_mux_4 (.sel(b0), .input0(b3), .input1(not_4_out), .out_4(two_input_mux_4_out_4));
  and and_1 (and_1_out, a0, b0);
  or or_1 (or_1_out, a0, b0);
  and and_2 (and_2_out, a1, b1);
  or or_2 (or_2_out, a1, b1);
  and and_3 (and_3_out, a2, b2);
  or or_3 (or_3_out, a2, b2);
  and and_4 (and_4_out, a3, b3);
  or or_4 (or_4_out, a3, b3);
  not not_5 (not_5_out, two_input_mux_4_out_4);
  four_bit_adder four_bit_adder_1 (
    .carryin(control0), .a0(a0), .b0(two_input_mux_1_out_4), .a1(a1), .b1(two_input_mux_2_out_4), .a2(a2),
    .b2(two_input_mux_3_out_4), .a3(a3), .b3(two_input_mux_4_out_4), .carryout(carryout),
    .result0(four_bit_adder_1_result0), .result1(four_bit_adder_1_result1),
    .result2(four_bit_adder_1_result2), .result3(four_bit_adder_1_result3));
  not not_6 (not_6_out, two_input_mux_1_out_4);
  not not_7 (not_7_out, two_input_mux_2_out_4);
  not not_8 (not_8_out, two_input_mux_3_out_4);
  four_input_mux four_input_mux_1 (
    .sel1(b0), .sel0(control0), .in0(and_1_out), .in1(or_1_out), .in2(four_bit_adder_1_result0),
    .in3(not_6_out), .out_7(result0));
  four_input_mux four_input_mux_2 (
    .sel1(b0), .sel0(control0), .in0(and_2_out), .in1(or_2_out), .in2(four_bit_adder_1_result1),
    .in3(not_7_out), .out_7(result1));
  four_input_mux four_input_mux_3 (
    .sel1(b0), .sel0(control0), .in0(and_3_out), .in1(or_3_out), .in2(four_bit_adder_1_result2),
    .in3(not_8_out), .out_7(result2));
  four_input_mux four_input_mux_4 (
    .sel1(b0), .sel0(control0), .in0(and_4_out), .in1(or_4_out), .in2(four_bit_adder_1_result3),
    .in3(not_5_out), .out_7(result3));

  assign control1 = b0;
endmodule
