// Logisim project 4_bit_register.circ as structural Verilog: 1 circuit, main circuit four_bit_register
module four_bit_register (
  input  writeenable,
  input  clock,
  input  data0,
  input  data1,
  input  data2,
  input  data3,
  output output0,
  output output1,
  output output2,
  output output3
);

  wire and_1_out, and_2_out, and_3_out, and_4_out;

  and and_1 (and_1_out, writeenable, data0);
  and and_2 (and_2_out, writeenable, data1);
  and and_3 (and_3_out, writeenable, data2);
  and and_4 (and_4_out, writeenable, data3);
  falling_edge_flip_flop falling_edge_flip_flop_1 (.clock(clock), .data(and_1_out), .Q(output0));
  falling_edge_flip_flop falling_edge_flip_flop_2 (.clock(clock), .data(and_2_out), .Q(output1));
  falling_edge_flip_flop falling_edge_flip_flop_3 (.clock(clock), .data(and_3_out), .Q(output2));
  falling_edge_flip_flop falling_edge_flip_flop_4 (.clock(clock), .data(and_4_out), .Q(output3));
endmodule
