// Logisim project 4_input_mux.circ as structural Verilog: 1 circuit, main circuit four_input_mux
module four_input_mux (
  input  sel1,
  input  sel0,
  input  in0,
  input  in1,
  input  in2,
  input  in3,
  output out_7
);

  wire and_1_out, and_2_out, and_3_out, and_5_out, not_1_out, not_2_out, not_3_out, not_4_out;

  not not_1 (not_1_out, sel0);
  not not_2 (not_2_out, sel1);
  and and_1 (and_1_out, not_1_out, not_2_out, in0);
  not not_3 (not_3_out, sel1);
  and and_2 (and_2_out, sel0, not_3_out, in1);
  not not_4 (not_4_out, sel0);
  and and_3 (and_3_out, not_4_out, sel1, in2);
  and and_4 (and_3_out, not_4_out, sel1, in2);
  and and_5 (and_5_out, sel0, sel1, in3);
  and and_6 (and_5_out, sel0, sel1, in3);
  or or_1 (out_7, and_1_out, and_2_out, and_3_out, and_5_out);
endmodule
