// Logisim project adder.circ as structural Verilog: 1 circuit, main circuit four_bit_adder
module four_bit_adder (
  input  carryin,
  input  a0,
  input  b0,
  input  a1,
  input  b1,
  input  a2,
  input  b2,
  input  a3,
  input  b3,
  output carryout,
  output result0,
  output result1,
  output result2,
  output result3
);

  wire a0b0_out, a0carryin_out, a1b1_out, a1carryin_out, and_1_out, and_2_out, and_3_out, and_4_out,
       and_5_out, and_6_out, and_7_out, and_8_out, and_9_out, and_10_out, and_11_out, and_12_out, and_13_out,
       and_14_out, and_15_out, and_16_out, and_17_out, and_18_out, and_19_out, and_20_out, and_21_out,
       and_22_out, and_23_out, and_24_out, and_25_out, and_26_out, and_27_out, and_28_out, and_29_out,
       and_30_out, and_31_out, and_32_out, and_33_out, and_34_out, and_35_out, and_36_out, and_37_out,
       and_38_out, b0carryin_out, b1carryin_out, not_1_out, not_2_out, not_3_out, not_4_out, not_5_out,
       not_6_out, not_7_out, not_8_out, not_9_out, not_10_out, not_11_out, not_12_out, not_13_out,
       not_14_out, not_15_out, not_16_out, not_17_out, not_18_out, not_19_out, not_20_out, not_21_out,
       not_22_out, not_23_out, not_24_out, or_1_out, or_2_out, or_3_out, or_4_out, or_5_out, or_6_out,
       or_7_out, or_8_out, or_9_out, or_10_out, or_11_out, or_12_out, or_13_out, or_14_out, or_15_out,
       or_16_out, or_17_out, or_19_out;

  and and_1 (and_1_out, carryin, not_1_out);
  not not_1 (not_1_out, a0);
  not not_2 (not_2_out, carryin);
  and and_2 (and_2_out, not_2_out, not_3_out);
  not not_3 (not_3_out, a0);
  and and_3 (and_3_out, a0, not_4_out);
  not not_4 (not_4_out, carryin);
  and and_4 (and_4_out, carryin, b0);
  and and_5 (and_5_out, carryin, not_5_out);
  not not_5 (not_5_out, a1);
  not not_6 (not_6_out, carryin);
  and and_6 (and_6_out, not_6_out, not_7_out);
  not not_7 (not_7_out, a1);
  and and_7 (and_7_out, a1, not_8_out);
  not not_8 (not_8_out, carryin);
  and and_8 (and_8_out, carryin, b1);
  and and_9 (and_9_out, carryin, not_9_out);
  not not_9 (not_9_out, a2);
  not not_10 (not_10_out, carryin);
  and and_10 (and_10_out, not_10_out, not_11_out);
  not not_11 (not_11_out, a2);
  and and_11 (and_11_out, a2, not_12_out);
  not not_12 (not_12_out, carryin);
  and and_12 (and_12_out, carryin, b2);
  and and_13 (and_13_out, carryin, not_13_out);
  not not_13 (not_13_out, a3);
  not not_14 (not_14_out, carryin);
  and and_14 (and_14_out, not_14_out, not_15_out);
  not not_15 (not_15_out, a3);
  and and_15 (and_15_out, a3, not_16_out);
  not not_16 (not_16_out, carryin);
  and and_16 (and_16_out, carryin, b3);
  and a0b0 (a0b0_out, a0, b0);
  and a0carryin (a0carryin_out, a0, carryin);
  and b0carryin (b0carryin_out, b0, carryin);
  and and_17 (and_17_out, and_1_out, not_17_out);
  not not_17 (not_17_out, b0);
  and and_18 (and_18_out, and_2_out, b0);
  and and_19 (and_19_out, and_3_out, not_18_out);
  not not_18 (not_18_out, b0);
  and and_20 (and_20_out, and_4_out, a0);
  and a1b1 (a1b1_out, a1, b1);
  and a1carryin (a1carryin_out, a1, carryin);
  and b1carryin (b1carryin_out, b1, carryin);
  and and_21 (and_21_out, and_5_out, not_19_out);
  not not_19 (not_19_out, b1);
  and and_22 (and_22_out, and_6_out, b1);
  and and_23 (and_23_out, and_7_out, not_20_out);
  not not_20 (not_20_out, b1);
  and and_24 (and_24_out, and_8_out, a1);
  and and_25 (and_25_out, a2, b2);
  and and_26 (and_26_out, a2, carryin);
  and and_27 (and_27_out, b2, carryin);
  and and_28 (and_28_out, and_9_out, not_21_out);
  not not_21 (not_21_out, b2);
  and and_29 (and_29_out, and_10_out, b2);
  and and_30 (and_30_out, and_11_out, not_22_out);
  not not_22 (not_22_out, b2);
  and and_31 (and_31_out, and_12_out, a2);
  and and_32 (and_32_out, a3, b3);
  and and_33 (and_33_out, a3, carryin);
  and and_34 (and_34_out, b3, carryin);
  and and_35 (and_35_out, and_13_out, not_23_out);
  not not_23 (not_23_out, b3);
  and and_36 (and_36_out, and_14_out, b3);
  and and_37 (and_37_out, and_15_out, not_24_out);
  not not_24 (not_24_out, b3);
  and and_38 (and_38_out, and_16_out, a3);
  or or_1 (or_1_out, a0b0_out, a0carryin_out);
  or or_2 (or_2_out, and_17_out, and_18_out);
  or or_3 (or_3_out, a1b1_out, a1carryin_out);
  or or_4 (or_4_out, and_21_out, and_22_out);
  or or_5 (or_5_out, and_25_out, and_26_out);
  or or_6 (or_6_out, and_28_out, and_29_out);
  or or_7 (or_7_out, and_32_out, and_33_out);
  or or_8 (or_8_out, and_35_out, and_36_out);
  or or_9 (or_9_out, or_1_out, b0carryin_out);
  or or_10 (or_10_out, or_2_out, and_19_out);
  or or_11 (or_11_out, or_3_out, b1carryin_out);
  or or_12 (or_12_out, or_4_out, and_23_out);
  or or_13 (or_13_out, or_5_out, and_27_out);
  or or_14 (or_14_out, or_6_out, and_30_out);
  or or_15 (or_15_out, or_7_out, and_34_out);
  or or_16 (or_16_out, or_8_out, and_37_out);
  or or_17 (or_17_out, or_13_out, or_15_out);
  or or_18 (result3, or_16_out, and_38_out);
  or or_19 (or_19_out, or_11_out, or_17_out);
  or or_20 (carryout, or_9_out, or_19_out);
  or or_21 (result1, or_12_out, and_24_out);
  or or_22 (result0, or_10_out, and_20_out);
  or or_23 (result2, or_14_out, and_31_out);
endmodule
