// Logisim project circuit.circ as structural Verilog: 1 circuit, main circuit circuit
module circuit (
  input  control0,
  input  control1,
  input  writeenable,
  input  in0,
  input  in1,
  input  in2,
  input  in3,
  output carryout,
  output output0,
  output output1,
  output output2,
  output output3
);

  wire clock_1_out, four_bit_register_1_output0, four_bit_register_1_output1, four_bit_register_1_output2,
       four_bit_register_1_output3, four_bit_register_2_output0, four_bit_register_2_output1,
       four_bit_register_2_output2, four_bit_register_2_output3, four_input_alu_1_result0,
       four_input_alu_1_result1, four_input_alu_1_result2, four_input_alu_1_result3;

  Clock clock_1 (.out(clock_1_out));
  four_bit_register four_bit_register_1 (
    .writeenable(writeenable), .clock(clock_1_out), .data0(in0), .data1(in1), .data2(in2), .data3(in3),
    .output0(four_bit_register_1_output0), .output1(four_bit_register_1_output1),
    .output2(four_bit_register_1_output2), .output3(four_bit_register_1_output3));
  four_bit_register four_bit_register_2 (
    .writeenable(writeenable), .clock(clock_1_out), .data0(in0), .data1(in1), .data2(in2), .data3(in3),
    .output0(four_bit_register_2_output0), .output1(four_bit_register_2_output1),
    .output2(four_bit_register_2_output2), .output3(four_bit_register_2_output3));
  four_bit_register four_bit_register_3 (
    .writeenable(writeenable), .clock(clock_1_out), .data0(four_input_alu_1_result0),
    .data1(four_input_alu_1_result1), .data2(four_input_alu_1_result2), .data3(four_input_alu_1_result3),
    .output0(output0), .output1(output1), .output2(output2), .output3(output3));
  four_input_ALU four_input_alu_1 (
    .control0(control0), .control1(control1), .a0(four_bit_register_1_output0),
    .b0(four_bit_register_1_output1), .a1(four_bit_register_1_output2), .b1(four_bit_register_1_output3),
    .a2(four_bit_register_2_output0), .b2(four_bit_register_2_output1), .a3(four_bit_register_2_output2),
    .b3(four_bit_register_2_output3), .result0(four_input_alu_1_result0), .result1(four_input_alu_1_result1),
    .result2(four_input_alu_1_result2), .result3(four_input_alu_1_result3), .carryout(carryout));
endmodule
