// Logisim project clocked_d_latch.circ as structural Verilog: 1 circuit, main circuit clocked_d_latch
module clocked_d_latch (
  input  clock,
  input  data,
  output Q
);

  wire and_1_out, and_2_out, not_1_out, not_3_out, or_1_out, or_2_out;

  not not_1 (not_1_out, data);
  and and_1 (and_1_out, clock, not_1_out);
  and and_2 (and_2_out, clock, data);
  or or_1 (or_1_out, and_1_out, not_3_out);
  not not_2 (Q, or_1_out);
  or or_2 (or_2_out, Q, and_2_out);
  not not_3 (not_3_out, or_2_out);
endmodule
