// Logisim project falling_edge_d_flip_flop.circ as structural Verilog: 1 circuit, main circuit falling_edge_flip_flop
module falling_edge_flip_flop (
  input  clock,
  input  data,
  output Q
);

  wire clocked_d_latch_1_q, not_1_out;

  not not_1 (not_1_out, clock);
  clocked_d_latch clocked_d_latch_1 (.clock(clock), .data(data), .Q(clocked_d_latch_1_q));
  clocked_d_latch clocked_d_latch_2 (.clock(not_1_out), .data(clocked_d_latch_1_q), .Q(Q));
endmodule
