// Logisim project one_bit_adder.circ as structural Verilog: 1 circuit, main circuit one_bit_adder
module one_bit_adder (
  input  carryin,
  input  a,
  input  b,
  output carryout,
  output result
);

  wire ab_out, acarryin_out, and_1_out, and_2_out, and_3_out, and_4_out, and_5_out, and_6_out, and_7_out,
       and_8_out, bcarryin_out, not_1_out, not_2_out, not_3_out, not_4_out, not_5_out, not_6_out, or_1_out,
       or_2_out, or_4_out;

  and and_1 (and_1_out, carryin, not_1_out);
  not not_1 (not_1_out, a);
  not not_2 (not_2_out, carryin);
  and and_2 (and_2_out, not_2_out, not_3_out);
  not not_3 (not_3_out, a);
  and and_3 (and_3_out, a, not_4_out);
  not not_4 (not_4_out, carryin);
  and and_4 (and_4_out, carryin, b);
  and ab (ab_out, a, b);
  and acarryin (acarryin_out, a, carryin);
  and bcarryin (bcarryin_out, b, carryin);
  and and_5 (and_5_out, and_1_out, not_5_out);
  not not_5 (not_5_out, b);
  and and_6 (and_6_out, and_2_out, b);
  and and_7 (and_7_out, and_3_out, not_6_out);
  not not_6 (not_6_out, b);
  and and_8 (and_8_out, and_4_out, a);
  or or_1 (or_1_out, ab_out, acarryin_out);
  or or_2 (or_2_out, and_5_out, and_6_out);
  or or_3 (carryout, or_1_out, bcarryin_out);
  or or_4 (or_4_out, or_2_out, and_7_out);
  or or_5 (result, or_4_out, and_8_out);
endmodule
