// Logisim project unclocked_latch.circ as structural Verilog: 1 circuit, main circuit unclocked_latch
module unclocked_latch (
  input  r,
  input  s,
  output Q,
  output NotQ
);

  wire or_1_out, or_2_out;

  or or_1 (or_1_out, r, NotQ);
  or or_2 (or_2_out, Q, s);
  not not_1 (Q, or_1_out);
  not not_2 (NotQ, or_2_out);
endmodule
